# Fritzing sketch BluetoothWeatherStation_V2 (saved by Fritzing 0.9.6b)
circuit board: 4.70334cm x 5.50996cm
breadboards: 1

parts:
  R1 = Resistor [tolerance=±5% resistance=100 power=0.25 package=THT]
  R2 = Resistor [tolerance=±5% resistance=220 power=0.25 package=THT]
  BMP180/BME280 = Barometric Pressure Sensor - BMP180 Breakout (GY-68)
  VCC1 = Battery
  Tensy_2_0 = PJRC Tensy 2.0
  R3 = Resistor [tolerance=±5% resistance=4.7k power=0.25 package=THT]
  R4 = Resistor [tolerance=±5% resistance=2.2k power=0.25 package=THT]
  LED1 = LED - 5mm [color="Red (633nm)" part_number="low voltage warning" current=0.030 package="5 mm [THT]"]
  HC_05 = Bluetooth HC-05 Macho [part_number="Hc 05"]
  Serial_Dev = Header 3 [package=screwterminal-3.5mm-3_lock.007s]

nets:
  N1: R1.Pin_0, R2.Pin_1, BMP180/BME280.VCC
  N2: R1.Pin_1, VCC1.+, Tensy_2_0.D9, R3.Pin_0, HC_05.VCC, Serial_Dev.1
  GND: R2.Pin_0, BMP180/BME280.GND, VCC1.-, Tensy_2_0.D10, R4.Pin_1, LED1.cathode, HC_05.GND, Serial_Dev.3
  N3: BMP180/BME280.SCL, Tensy_2_0.A2
  N4: BMP180/BME280.SDA, Tensy_2_0.A3
  N5: Tensy_2_0.VCC, HC_05.TXD
  N6: Tensy_2_0.RAW, Serial_Dev.2
  N7: Tensy_2_0.RESET, HC_05.RXD
  N8: Tensy_2_0.SCK, R3.Pin_1, R4.Pin_0
  N9: Tensy_2_0.MISO, LED1.anode

notes:
  Bluetooth Weather Sensor V2.0.0 B. Fritz 2021. CC BY-NC-SA 2.5
  Low voltage
  TX
  RX
  Serial Input
  SDA
  SCL
  Vltg low
  Vltg low out
  100
  220
  4,7 k
  2,2 k
  +
  -
  Serinal in

custom parts:
  PJRC Tensy 2.0: approach to Arduino. This is a 5V Arduino running the 16MHz bootloader. Arduino Pro Mini does not come with connectors populated so that you can solder in any connector or wire with any orientation you need. We recommend first time Arduino users start with the Uno R3. It's a great board that will get you up and running quickly. The Arduino Pro series is meant for users that understand the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
